# Fritzing sketch sketch (saved by Fritzing 0.9.6b)
breadboards: 1

parts:
  Raspberry_Pi_1 = Raspberry Pi 3 [part_number=RPI-3-V1.2]
  R1 = Resistor [tolerance=±5% resistance=10k package="2010 [SMD]"]
  IRLB8721 = Basic FET N-Channel [package="D2Pak [SMD]"]
  IRLB8722 = Basic FET N-Channel [package="D2Pak [SMD]"]
  R2 = Resistor [tolerance=±5% resistance=10k package="2010 [SMD]"]
  Warm_White = LEDs [package=led-1206]
  Cool_White = LEDs [package=led-1206]
  12V = Power plug

nets:
  N1: Raspberry_Pi_1.GIPO13, R1.Pin_0, IRLB8721.Gate
  GND: Raspberry_Pi_1.GND, R1.Pin_1, IRLB8721.source, IRLB8722.source, R2.Pin_1, 12V.GND
  N2: Raspberry_Pi_1.GIPO12, IRLB8722.Gate, R2.Pin_0
  N3: IRLB8721.drain, Cool_White.A
  N4: IRLB8722.drain, Warm_White.A
  N5: Warm_White.C, Cool_White.C, 12V.VCC
